# Fritzing sketch arduino (saved by Fritzing 0.8.7b)

parts:
  Composant1 = Arduino Uno (Rev3)
  J1 = female pin header, 2 pins [form="♀ (female)"]
  J2 = female pin header, 2 pins [form="♀ (female)"]
  J3 = single row smd female pin header, 1 pin [form="♀ (female)"]
  J4 = single row smd female pin header, 1 pin [form="♀ (female)"]
  J5 = female pin header, 2 pins [form="♀ (female)"]
  J6 = female pin header, 2 pins [form="♀ (female)"]
  J7 = single row smd female pin header, 1 pin [form="♀ (female)"]

nets:
  N1: Composant1.A0, J7.pin1
  N2: Composant1.A5/SCL, Composant1.A4/SDA, J5.pin1, J5.pin2, J6.pin1, J6.pin2
  N3: Composant1.D2, J1.pin1
  N4: Composant1.D3_PWM, J1.pin2
  N5: Composant1.D4, J4.pin1
  N6: Composant1.D5_PWM, J2.pin1
  N7: Composant1.D6_PWM, J2.pin2
  N8: Composant1.D7, J3.pin1

notes:
  SHT31
  DHT22
  GROOVE LCD
  LORA E5
  ULTRASONIC RANGER
  SEN HX711
  BATERRY LVL
  SCL
  SDA
