# Fritzing sketch stm32 (saved by Fritzing 0.9.3b)

parts:
  J1 = STM32 Nucleo boards
  LoRa1 = LoRa-e5
  SHT1 = SHT31_Grove
  SEN-HX1 = SEN-HX711
  A1 = DHT22 module
  R1 = Resistor [tolerance=±5% resistance=1k package="0805 [SMD]"]
  R2 = Resistor [tolerance=±5% resistance=1k package="0805 [SMD]"]  # not connected
  R3 = Resistor [tolerance=±5% resistance=1k package="0805 [SMD]"]
  PIR1 = PIR_grove
  U1 = LIPO-1000mAh [package=lipo-1000]

nets:
  N1: J1.A0, LoRa1.TX
  N2: J1.A1, LoRa1.RX
  N3: J1.A2, R1.Pin_0, R3.Pin_0
  N4: J1.E5V, R3.Pin_1, U1.+
  N5: J1.A4/SDA, SHT1.SDA
  N6: J1.A5/SCL, SHT1.SCL
  N7: J1.D3_PWM, PIR1.D1
  N8: J1.D4, A1.DAT
  N9: J1.D6_PWM, SEN-HX1.DT
  N10: J1.D7, SEN-HX1.SCK
  3V3: J1.3V3, SHT1.VDD

custom parts:
  SHT31_Grove: SHT31 Jumidity Température
  SEN-HX711: SEN-HX711 Jauge de contraintes
  DHT22 module: DHT22 module. Pins GND VCC Data.
  PIR_grove: PIR Motion Sensor V1.2 grove
